# Fritzing sketch esp-01_Arduino_a3(1) (saved by Fritzing 0.9.3b)
circuit board: 7.29073cm x 4.16358cm
perfboards: 1

parts:
  R2 = Resistor [tolerance=±5% resistance=330 package=THT]
  J2 = male pin header, 5 pins [form="♂ (male)"]
  U1 = atmega328 [package=dip]
  C1 = Capacitor [package=cap-pth-small2]
  C2 = Capacitor [package=cap-pth-small2]
  J5 = male pin header, 6 pins [form="♂ (male)"]
  J3 = male pin header, 4 pins [form="♂ (male)"]
  J4 = male pin header, 4 pins [form="♂ (male)"]
  J7 = male pin header, 2 pins [form="♂ (male)"]
  XTAL1 = Crystal [frequency="16 Mhz" package=THT]
  R1 = Resistor [tolerance=±10% resistance=10k package=THT]
  J6 = male pin header, 2 pins [form="♂ (male)"]
  U3 = V_REG_LD1117VXX [package=78xxl]
  LED1 = LED - 3mm [color="Red (633nm)" package="3 mm [THT]"]
  U2 = ESP8266 WiFi Module [part_number=ESP8266]
  R3 = Resistor [tolerance=±10% resistance=10k package=THT]
  J1 = male pin header, 5 pins [form="♂ (male)"]
  S1 = Pushbutton [package="[THT]"]
  R4 = Resistor [tolerance=±10% resistance=10k package=THT]
  J8 = female pin header, 2 pins [form="♀ (female)"]
  J9 = female pin header, 2 pins [form="♀ (female)"]
  J10 = female pin header, 2 pins [form="♀ (female)"]
  J11 = female pin header, 1 pin [form="♀ (female)"]  # not connected
  J12 = female pin header, 1 pin [form="♀ (female)"]  # not connected
  J13 = female pin header, 1 pin [form="♀ (female)"]  # not connected
  J14 = female pin header, 1 pin [form="♀ (female)"]  # not connected

nets (from the pcb view):
  N1: R2.Pin_0, U1.D13
  N2: R2.Pin_1, LED1.anode
  N3: J2.pin1, U1.D0_(RX), J1.pin3
  N4: J2.pin2, U1.D1_(TX), J1.pin2
  N5: J2.pin3, U1.D2
  N6: J2.pin4, U1.D3_(PWM)
  N7: J2.pin5, U1.D4
  N8: U1.RESET, S1.Pin_1, S1.Pin_2
  N9: U1.VCC, U1.AVCC, U1.AREF, R1.Pin_1, J6.pin1, J6.pin2, U3.IN, J1.pin5
  N10: U1.GND#7, C1.1, C2.2, J7.pin1, J7.pin2, U3.GND, LED1.cathode, J1.pin4, S1.Pin_3, S1.Pin_4, J8.pin2, J10.pin1
  N11: U1.XLAT1, C2.1, XTAL1.pin_1
  N12: U1.XLAT2, C1.2, XTAL1.pin_0
  N13: U1.D5_(PWM), J3.pin1
  N14: U1.D6_(PWM), J3.pin2
  N15: U1.D7, J3.pin3, U2.RXD
  N16: U1.D8, J3.pin4, U2.TXD
  N17: U1.D9_(PWM), J4.pin4
  N18: U1.D10_(PWM), J4.pin3
  N19: U1.D11_(PWM), J4.pin2
  N20: U1.D12, J4.pin1
  N21: U1.A0, J5.pin6
  N22: U1.A1, J5.pin5
  N23: U1.A2, J5.pin4
  N24: U1.A3, J5.pin3
  N25: U1.A4, J5.pin2
  N26: U1.A5, J5.pin1
  N27: R1.Pin_0, J1.pin1
  N28: U3.OUT, U2.VCC, R3.Pin_0, R4.Pin_0
  N29: U2.GPIO_0, J9.pin1
  N30: U2.RST, R4.Pin_1, J8.pin1
  N31: U2.GPIO_2, J9.pin2
  N32: U2.CH_PD, R3.Pin_1
  N33: U2.GND, J10.pin2

notes:
  RST
  TX
  RX
  GND
  2020 TVTC328V1
  +
  -
  5V
  VCC
  Vcc
  GPIO2
  GPIO0
  PD
  3.3V

custom parts:
  ESP8266 WiFi Module: Generic WiFi Module based on the ESP8266 with onboard PCB antenna and UART communications
