# Fritzing sketch esp-01_a4 (saved by Fritzing 0.9.3b)
circuit board: 7.30277cm x 4.90954cm
perfboards: 1

parts:
  U1 = V_REG_LD1117VXX [part_number=LD1117 package=78xxl]
  J1 = male pin header, 8 pins [form="♂ (male)"]
  U3 = ESP8266 WiFi Module [part_number=ESP8266]
  S1 = Pushbutton [package="[THT]"]
  R2 = Resistor [tolerance=±5% resistance=10k package=THT]
  R1 = Resistor [tolerance=±5% resistance=10k package=THT]
  R3 = Resistor [tolerance=±5% resistance=330 package=THT]
  R4 = Resistor [tolerance=±5% resistance=330 package=THT]
  J3 = male pin header, 1 pin [form="♂ (male)"]
  J4 = male pin header, 1 pin [form="♂ (male)"]  # not connected
  LED2 = LED - 5mm [color="Red (633nm)" package="5 mm [THT]"]
  LED1 = LED - 5mm [color="Red (633nm)" package="5 mm [THT]"]
  S2 = Toggle Switch [package=THT]
  J2 = male pin header, 4 pins [form="♂ (male)"]
  C1 = Ceramic Capacitor [capacitance=100nF package="100 mil [THT, multilayer]"]
  S3 = SWITCH-DPDT [package=gpi-152-3013]
  Q1 = NPN-Transistor [package="TO92 [THT]"]
  IR1 = LED - 5mm [color="Red (633nm)" package="5 mm [THT]"]
  IR2 = LED - 5mm [color="Red (633nm)" package="5 mm [THT]"]
  R5 = Resistor [tolerance=±5% resistance=10 package=THT]
  J5 = female pin header, 1 pin [form="♀ (female)"]  # not connected
  J6 = female pin header, 1 pin [form="♀ (female)"]  # not connected
  J7 = female pin header, 1 pin [form="♀ (female)"]  # not connected
  J8 = female pin header, 1 pin [form="♀ (female)"]  # not connected

nets (from the pcb view):
  N1: U1.OUT, U3.VCC, R2.Pin_0, R1.Pin_0, R3.Pin_0, R4.Pin_0, IR1.anode
  GND: U1.GND, J1.pin3, J1.pin4, U3.GND, S1.Pin_1, S1.Pin_2, S2.COM, J2.pin2, C1.0
  N2: U1.IN, J1.pin5, J1.pin6, J3.pin1, J2.pin1
  N3: J1.pin1, U3.TXD, J2.pin4
  N4: J1.pin2, U3.RXD, J2.pin3
  N5: J1.pin7, U3.GPIO_2, LED2.cathode, R5.Pin_1
  N6: J1.pin8, U3.GPIO_0, LED1.cathode, S2.L2, S3.3
  N7: U3.RST, S1.Pin_3, S1.Pin_4, R2.Pin_1, S2.L1
  N8: U3.CH_PD, R1.Pin_1
  N9: R3.Pin_1, LED1.anode
  N10: R4.Pin_1, LED2.anode
  N11: S3.2, Q1.E
  N12: Q1.B, R5.Pin_0
  N13: Q1.C, IR2.cathode
  N14: IR1.cathode, IR2.anode

notes:
  TX-GND
  PD-GP2
  RST-GP0
  VCC-RX
  5V
  GND
  3.3V
  TX
  RX
  GPIO2
  GPIO0
  2020 TVTCC_ESP01V1.0 NiTL/KuoWC
  +
  -
  PD
  RST
  2N3904

custom parts:
  ESP8266 WiFi Module: Generic WiFi Module based on the ESP8266 with onboard PCB antenna and UART communications
