# Fritzing sketch Untitled Sketch (saved by Fritzing 0.9.3b)
breadboards: 1

parts:
  U1 = atmega328 [package=dip]
  LED1 = LED - 5mm [color="Red (633nm)" package="5 mm [THT]"]
  S1 = Pushbutton [package="[THT]"]
  XTAL1 = Crystal [frequency="16 Mhz" package=THT]
  C1 = Capacitor [package=cap-pth-small2]
  C2 = Capacitor [package=cap-pth-small2]
  R1 = Resistor [tolerance=±5% resistance=10k package=THT]
  R2 = Resistor [tolerance=±5% resistance=220 package=THT]
  J1 = male pin header, 2 pins [form="♂ (male)"]
  J2 = male pin header, 2 pins [form="♂ (male)"]

nets:
  N1: U1.RESET, U1.GND#7, LED1.cathode, S1.Pin_1, S1.Pin_2, C1.2, C2.2, R1.Pin_1, J2.pin2
  N2: U1.D0_(RX), J1.pin1
  N3: U1.D1_(TX), J1.pin2
  N4: U1.VCC, R1.Pin_0, J2.pin1
  N5: U1.XLAT1, XTAL1.pin_1, C1.1
  N6: U1.XLAT2, XTAL1.pin_0, C2.1
  N7: U1.D13, R2.Pin_0
  N8: LED1.anode, R2.Pin_1
  N9: S1.Pin_3, S1.Pin_4

notes:
  VCC
  GND
